// Logisim project Lab 2 Given.circ as structural Verilog: 6 circuits, main circuit Main
module Main (
);

  wire alu_1_zero, ALUSrc, and_1_out, ANDI, Branch, CLK, control_unit_1_aluop0, control_unit_1_aluop1, JAL,
       Jmp, JR, MemRead, MemToReg, MemWrite, RegDst, RegWrite, WrReg;
  wire [2:0] alu_control_1_aluop3;
  wire [3:0] ALUCntrl, multiplexer_4_out;
  wire [4:0] multiplexer_2_out, WrAddr;
  wire [5:0] Funct, OpCntrl;
  wire [25:6] rom_1_data;
  wire [27:0] adder_1_out;
  wire [31:0] adder_2_out, alu_1_aluresult, bit_extender_2_out, JALValue, JRValue, Jump, MemData,
       multiplexer_6_out, multiplexer_8_out, multiplexer_9_out, multiplexer_11_out, NextPC, PC, ram_1_data,
       Write_Data;

  Clock clock_1 (.out(CLK));
  Register #(.width(32)) Program_Counter (.D(NextPC), .Q(PC), .clk(CLK));  // open: en, clr
  Adder #(.width(32)) adder_1 (.a(PC), .b(32'h1), .out({Jump[31:28], adder_1_out}));  // open: cin, cout
  Shifter #(.width(28)) shifter_1 (.\dist (5'b00010));  // open: in, out
  Control_Unit control_unit_1 (
    .Op5(OpCntrl[5]), .Op4(OpCntrl[4]), .Op3(OpCntrl[3]), .Op2(OpCntrl[2]), .Op1(OpCntrl[1]),
    .Op0(OpCntrl[0]), .RegDst(RegDst), .Branch(Branch), .MemRead(MemRead), .MemToReg(MemToReg),
    .MemWrite(MemWrite), .ALUSrc(ALUSrc), .RegWrite(RegWrite), .Jmp(Jmp), .JAL(JAL),
    .ALUOp1(control_unit_1_aluop1), .ALUOp0(control_unit_1_aluop0), .ANDI(ANDI));
  assign Jump[27:0] = {{2{1'b0}}, {rom_1_data, Funct}};  // Bit_Extender bit_extender_1
  ROM #(.dataWidth(32)) rom_1 (.addr(PC[7:0]), .data({OpCntrl, rom_1_data, Funct}));  // open: sel
  Multiplexer #(.width(32), .enable("false")) multiplexer_1 (
    .in1({Jump[31:28], adder_1_out}), .out(JALValue), .sel(JAL));  // open: in0
  ALU_Control alu_control_1 (
    .ALUOp1(control_unit_1_aluop1), .ALUOp0(control_unit_1_aluop0), .Funt1(Funct[3]), .Funt2(Funct[2]),
    .Funt3(Funct[1]), .Funt4(Funct[0]), .ALUop1_2(alu_control_1_aluop3[2]), .ALUop2(alu_control_1_aluop3[1]),
    .ALUop3(alu_control_1_aluop3[0]), .JR(JR));
  Multiplexer #(.width(5), .enable("false")) multiplexer_2 (
    .in0(rom_1_data[20:16]), .in1(rom_1_data[15:11]), .out(multiplexer_2_out), .sel(RegDst));
  assign bit_extender_2_out = {{16{1'b0}}, {rom_1_data[15:6], Funct}};  // Bit_Extender bit_extender_2
  Register_File register_file_1 (
    .WrAddr(WrAddr), .WrData(Write_Data), .WrReg(WrReg), .RdAddr1(rom_1_data[25:21]),
    .RdAddr2(rom_1_data[20:16]), .RdData1(JRValue), .RdData2(MemData), .Clock(CLK));
  Multiplexer #(.width(5), .enable("false")) multiplexer_3 (
    .in0(multiplexer_2_out), .in1({5{1'b1}}), .out(WrAddr), .sel(JAL));
  Multiplexer #(.width(4), .enable("false")) multiplexer_4 (
    .in0({1'b0, alu_control_1_aluop3}), .in1(4'b0101), .out(multiplexer_4_out), .sel(Branch));
  Multiplexer #(.enable("false")) multiplexer_5 (.in0(RegWrite), .in1(1'b0), .out(WrReg), .sel(JR));
  Multiplexer #(.width(32), .enable("false")) multiplexer_6 (
    .in0(MemData), .in1(bit_extender_2_out), .out(multiplexer_6_out), .sel(ALUSrc));
  Multiplexer #(.width(4), .enable("false")) multiplexer_7 (
    .in0(multiplexer_4_out), .in1(4'b0011), .out(ALUCntrl), .sel(ANDI));
  Shifter #(.width(32)) shifter_2 (.\dist (5'b00010));  // open: in, out
  ALU alu_1 (
    .ALUCtl(ALUCntrl), .A(JRValue), .B(multiplexer_6_out), .ALUResult(alu_1_aluresult), .Zero(alu_1_zero));  // open: Overflow, Shamt
  Shifter #(.width(32)) shifter_3 ();  // open: in, dist, out
  Adder #(.width(32)) adder_2 (
    .a({Jump[31:28], adder_1_out}), .b(bit_extender_2_out), .out(adder_2_out));  // open: cin, cout
  and and_1 (and_1_out, Branch, alu_1_zero);
  Multiplexer #(.width(32), .enable("false")) multiplexer_8 (
    .in0({Jump[31:28], adder_1_out}), .in1(adder_2_out), .out(multiplexer_8_out), .sel(and_1_out));
  Multiplexer #(.width(32), .enable("false")) multiplexer_9 (
    .in0(multiplexer_8_out), .in1(Jump), .out(multiplexer_9_out), .sel(Jmp));
  RAM #(.dataWidth(32), .bus("separate")) ram_1 (
    .addr(alu_1_aluresult[7:0]), .din(MemData), .data(ram_1_data), .str(MemWrite), .clk(CLK), .ld(MemRead));  // open: sel, clr
  Multiplexer #(.width(32), .enable("false")) multiplexer_10 (
    .in0(multiplexer_9_out), .in1(JRValue), .out(NextPC), .sel(JR));
  Multiplexer #(.width(32), .enable("false")) multiplexer_11 (
    .in0(alu_1_aluresult), .in1(ram_1_data), .out(multiplexer_11_out), .sel(MemToReg));
  Multiplexer #(.width(32), .enable("false")) multiplexer_12 (
    .in0(multiplexer_11_out), .in1(JALValue), .out(Write_Data), .sel(JAL));
  // Probe on PC
  // Probe on Branch
  // Probe on Jmp
  // Probe on JAL
  // Probe on JR
  // Probe on WrReg
  // Probe on WrAddr
  // Probe on Write_Data
  // Probe on MemWrite
  // Probe on MemData

  // Notes on the sheet:
  //   Instruction Memory
  //   contents of rom_1 (hex, n*v repeats v):
  //   20010008 34220005 3043ffff 232020 832822 223024 663826 aca40064 8ca80064 22482a c95025 a95827
  //   161602b 296d0001 c000010 201b0001 200e0001 23ff001c 11c00003 1c97022 8000012 201c0001 3e00008
  //   201d0001 201e0001
  //   Data Memory
endmodule

module ALU (
  input  [3:0] ALUCtl,
  input  [31:0] A,
  input  [31:0] B,
  input  [4:0] Shamt,
  output [31:0] ALUResult,
  output Zero,
  output Overflow
);

  wire comparator_1_lt, comparator_2_lt, comparator_3_eq, comparator_4_eq, or_2_out;
  wire [31:0] ADD, AND, NOR, OR, SLL, SLT, SLTU, SRL, SUB, XOR;

  // Probe on ALUCtl
  assign NOR = ~(A | B);  // NOR_Gate nor_1, 32 bits wide
  Adder #(.width(32)) adder_1 (.a(A), .b(B), .out(ADD));  // open: cin, cout
  Subtractor #(.width(32)) subtractor_1 (.a(A), .b(B), .out(SUB));  // open: bin, bout
  assign AND = A & B;  // AND_Gate and_1, 32 bits wide
  assign OR = A | B;  // OR_Gate or_1, 32 bits wide
  assign XOR = A ^ B;  // XOR_Gate xor_1, 32 bits wide
  Comparator #(.width(32)) comparator_1 (.a(A), .b(B), .lt(comparator_1_lt));  // open: gt, eq
  assign SLT = {{31{1'b0}}, comparator_1_lt};  // Bit_Extender bit_extender_1
  Shifter #(.width(32)) shifter_1 (.in(B), .\dist (Shamt), .out(SLL));
  Shifter #(.width(32), .shift("lr")) shifter_2 (.in(B), .\dist (Shamt), .out(SRL));
  Comparator #(.width(32), .mode("unsigned")) comparator_2 (.a(A), .b(B), .lt(comparator_2_lt));  // open: gt, eq
  assign SLTU = {{31{1'b0}}, comparator_2_lt};  // Bit_Extender bit_extender_2
  Multiplexer #(.select(4), .width(32), .enable("false")) multiplexer_1 (
    .in0(XOR), .in1(SLTU), .in2(SLT), .in3(AND), .in4(NOR), .in5(SUB), .in6(OR), .in7(ADD), .in8(SRL),
    .in9(SLL), .out(ALUResult), .sel(ALUCtl));  // open: in10, in11, in12, in13, in14, in15
  Comparator #(.width(4)) comparator_3 (.a(4'b0111), .b(ALUCtl), .eq(comparator_3_eq));  // open: gt, lt
  Comparator #(.width(4)) comparator_4 (.a(ALUCtl), .b(4'b0101), .eq(comparator_4_eq));  // open: gt, lt
  Overflow_Unit overflow_unit_1 (
    .Add(comparator_3_eq), .Sub(comparator_4_eq), .ASign(A[31]), .BSign(B[31]), .ResultSign(ALUResult[31]),
    .Overflow(Overflow));
  or or_2 (or_2_out, ALUResult[0], ALUResult[1], ALUResult[2], ALUResult[3], ALUResult[4], ALUResult[5], ALUResult[6], ALUResult[7], ALUResult[8], ALUResult[9], ALUResult[10], ALUResult[11], ALUResult[12], ALUResult[13], ALUResult[14], ALUResult[15], ALUResult[16], ALUResult[17], ALUResult[18], ALUResult[19], ALUResult[20], ALUResult[21], ALUResult[22], ALUResult[23], ALUResult[24], ALUResult[25], ALUResult[26], ALUResult[27], ALUResult[28], ALUResult[29], ALUResult[30], ALUResult[31]);
  not not_1 (Zero, or_2_out);

  // Other names for the same wires on the sheet: ASign = A[31]; ResultSign = ALUResult[31]; BSign = B[31]

  // Notes on the sheet:
  //   ALUCtl for ADD for top port
  //   ALUCtl for SUB for second port
endmodule

module Register_File (
  input  [4:0] WrAddr,
  input  [31:0] WrData,
  input  WrReg,
  input  [4:0] RdAddr1,
  input  [4:0] RdAddr2,
  input  Clock,
  output [31:0] RdData1,
  output [31:0] RdData2
);

  wire WrReg0, WrReg1, WrReg2, WrReg3, WrReg4, WrReg5, WrReg6, WrReg7, WrReg8, WrReg9, WrReg10, WrReg11,
       WrReg12, WrReg13, WrReg14, WrReg15, WrReg16, WrReg17, WrReg18, WrReg19, WrReg20, WrReg21, WrReg22,
       WrReg23, WrReg24, WrReg25, WrReg26, WrReg27, WrReg28, WrReg29, WrReg30, WrReg31;
  wire [31:0] RegData1, RegData2, RegData3, RegData4, RegData5, RegData6, RegData7, RegData8, RegData9,
       RegData10, RegData11, RegData12, RegData13, RegData14, RegData15, RegData16, RegData17, RegData18,
       RegData19, RegData20, RegData21, RegData22, RegData23, RegData24, RegData25, RegData26, RegData27,
       RegData28, RegData29, RegData30, RegData31;

  Demultiplexer #(.select(5), .enable("false")) demultiplexer_1 (
    .out0(WrReg0), .out1(WrReg1), .out2(WrReg2), .out3(WrReg3), .out4(WrReg4), .out5(WrReg5), .out6(WrReg6),
    .out7(WrReg7), .out8(WrReg8), .out9(WrReg9), .out10(WrReg10), .out11(WrReg11), .out12(WrReg12),
    .out13(WrReg13), .out14(WrReg14), .out15(WrReg15), .out16(WrReg16), .out17(WrReg17), .out18(WrReg18),
    .out19(WrReg19), .out20(WrReg20), .out21(WrReg21), .out22(WrReg22), .out23(WrReg23), .out24(WrReg24),
    .out25(WrReg25), .out26(WrReg26), .out27(WrReg27), .out28(WrReg28), .out29(WrReg29), .out30(WrReg30),
    .out31(WrReg31), .in(WrReg), .sel(WrAddr));
  // Probe on RegData4
  Register #(.width(32)) Reg4 (.D(WrData), .en(WrReg4), .Q(RegData4), .clk(Clock));  // open: clr
  // Probe on RegData8
  Register #(.width(32)) Reg8 (.D(WrData), .en(WrReg8), .Q(RegData8), .clk(Clock));  // open: clr
  // Probe on RegData12
  Register #(.width(32)) Reg12 (.D(WrData), .en(WrReg12), .Q(RegData12), .clk(Clock));  // open: clr
  // Probe on RegData16
  Register #(.width(32)) Reg16 (.D(WrData), .en(WrReg16), .Q(RegData16), .clk(Clock));  // open: clr
  // Probe on RegData20
  Register #(.width(32)) Reg20 (.D(WrData), .en(WrReg20), .Q(RegData20), .clk(Clock));  // open: clr
  // Probe on RegData24
  Register #(.width(32)) Reg24 (.D(WrData), .en(WrReg24), .Q(RegData24), .clk(Clock));  // open: clr
  // Probe on RegData28
  Register #(.width(32)) Reg28 (.D(WrData), .en(WrReg28), .Q(RegData28), .clk(Clock));  // open: clr
  Register #(.width(32)) Reg1 (.D(WrData), .en(WrReg1), .Q(RegData1), .clk(Clock));  // open: clr
  Register #(.width(32)) Reg5 (.D(WrData), .en(WrReg5), .Q(RegData5), .clk(Clock));  // open: clr
  Register #(.width(32)) Reg9 (.D(WrData), .en(WrReg9), .Q(RegData9), .clk(Clock));  // open: clr
  Register #(.width(32)) Reg13 (.D(WrData), .en(WrReg13), .Q(RegData13), .clk(Clock));  // open: clr
  Register #(.width(32)) Reg17 (.D(WrData), .en(WrReg17), .Q(RegData17), .clk(Clock));  // open: clr
  Register #(.width(32)) Reg21 (.D(WrData), .en(WrReg21), .Q(RegData21), .clk(Clock));  // open: clr
  Register #(.width(32)) Reg25 (.D(WrData), .en(WrReg25), .Q(RegData25), .clk(Clock));  // open: clr
  Register #(.width(32)) Reg29 (.D(WrData), .en(WrReg29), .Q(RegData29), .clk(Clock));  // open: clr
  // Probe on RegData1
  // Probe on RegData5
  // Probe on RegData9
  // Probe on RegData13
  // Probe on RegData17
  // Probe on RegData21
  // Probe on RegData25
  // Probe on RegData29
  // Probe on RegData2
  Register #(.width(32)) Reg2 (.D(WrData), .en(WrReg2), .Q(RegData2), .clk(Clock));  // open: clr
  // Probe on RegData6
  Register #(.width(32)) Reg6 (.D(WrData), .en(WrReg6), .Q(RegData6), .clk(Clock));  // open: clr
  // Probe on RegData10
  Register #(.width(32)) Reg10 (.D(WrData), .en(WrReg10), .Q(RegData10), .clk(Clock));  // open: clr
  // Probe on RegData14
  Register #(.width(32)) Reg14 (.D(WrData), .en(WrReg14), .Q(RegData14), .clk(Clock));  // open: clr
  // Probe on RegData18
  Register #(.width(32)) Reg18 (.D(WrData), .en(WrReg18), .Q(RegData18), .clk(Clock));  // open: clr
  // Probe on RegData22
  Register #(.width(32)) Reg22 (.D(WrData), .en(WrReg22), .Q(RegData22), .clk(Clock));  // open: clr
  // Probe on RegData26
  Register #(.width(32)) Reg26 (.D(WrData), .en(WrReg26), .Q(RegData26), .clk(Clock));  // open: clr
  // Probe on RegData30
  Register #(.width(32)) Reg30 (.D(WrData), .en(WrReg30), .Q(RegData30), .clk(Clock));  // open: clr
  // Probe on RegData3
  Register #(.width(32)) Reg3 (.D(WrData), .en(WrReg3), .Q(RegData3), .clk(Clock));  // open: clr
  // Probe on RegData7
  Register #(.width(32)) Reg7 (.D(WrData), .en(WrReg7), .Q(RegData7), .clk(Clock));  // open: clr
  // Probe on RegData11
  Register #(.width(32)) Reg11 (.D(WrData), .en(WrReg11), .Q(RegData11), .clk(Clock));  // open: clr
  // Probe on RegData15
  Register #(.width(32)) Reg15 (.D(WrData), .en(WrReg15), .Q(RegData15), .clk(Clock));  // open: clr
  // Probe on RegData19
  Register #(.width(32)) Reg19 (.D(WrData), .en(WrReg19), .Q(RegData19), .clk(Clock));  // open: clr
  // Probe on RegData23
  Register #(.width(32)) Reg23 (.D(WrData), .en(WrReg23), .Q(RegData23), .clk(Clock));  // open: clr
  // Probe on RegData27
  Register #(.width(32)) Reg27 (.D(WrData), .en(WrReg27), .Q(RegData27), .clk(Clock));  // open: clr
  // Probe on RegData31
  Register #(.width(32)) Reg31 (.D(WrData), .en(WrReg31), .Q(RegData31), .clk(Clock));  // open: clr
  Multiplexer #(.select(5), .width(32), .enable("false")) multiplexer_1 (
    .in0({32{1'b0}}), .in1(RegData1), .in2(RegData2), .in3(RegData3), .in4(RegData4), .in5(RegData5),
    .in6(RegData6), .in7(RegData7), .in8(RegData8), .in9(RegData9), .in10(RegData10), .in11(RegData11),
    .in12(RegData12), .in13(RegData13), .in14(RegData14), .in15(RegData15), .in16(RegData16),
    .in17(RegData17), .in18(RegData18), .in19(RegData19), .in20(RegData20), .in21(RegData21),
    .in22(RegData22), .in23(RegData23), .in24(RegData24), .in25(RegData25), .in26(RegData26),
    .in27(RegData27), .in28(RegData28), .in29(RegData29), .in30(RegData30), .in31(RegData31), .out(RdData1),
    .sel(RdAddr1));
  Multiplexer #(.select(5), .width(32), .enable("false")) multiplexer_2 (
    .in0({32{1'b0}}), .in1(RegData1), .in2(RegData2), .in3(RegData3), .in4(RegData4), .in5(RegData5),
    .in6(RegData6), .in7(RegData7), .in8(RegData8), .in9(RegData9), .in10(RegData10), .in11(RegData11),
    .in12(RegData12), .in13(RegData13), .in14(RegData14), .in15(RegData15), .in16(RegData16),
    .in17(RegData17), .in18(RegData18), .in19(RegData19), .in20(RegData20), .in21(RegData21),
    .in22(RegData22), .in23(RegData23), .in24(RegData24), .in25(RegData25), .in26(RegData26),
    .in27(RegData27), .in28(RegData28), .in29(RegData29), .in30(RegData30), .in31(RegData31), .out(RdData2),
    .sel(RdAddr2));
endmodule

module Overflow_Unit (
  input  Add,
  input  Sub,
  input  ASign,
  input  BSign,
  input  ResultSign,
  output Overflow
);

  wire and_1_out, and_2_out, or_1_out, xnor_1_out, xor_1_out, xor_2_out;

  xnor xnor_1 (xnor_1_out, ASign, BSign);
  xor xor_1 (xor_1_out, ASign, BSign);
  and and_1 (and_1_out, xnor_1_out, Add);
  and and_2 (and_2_out, xor_1_out, Sub);
  or or_1 (or_1_out, and_1_out, and_2_out);
  xor xor_2 (xor_2_out, ResultSign, ASign);
  and and_3 (Overflow, or_1_out, xor_2_out);

  // Notes on the sheet:
  //   Overflow occurs when doing addition and sign(A) == sign(B) && sign(result) != sign(A)
  //   Or
  //   Overflow occurs when doing subtraction and sign(A) != sign(B) && sign(result) != sign(A)
endmodule

module Control_Unit (
  input  Op5,
  input  Op4,
  input  Op3,
  input  Op2,
  input  Op1,
  input  Op0,
  output RegDst,
  output Branch,
  output MemRead,
  output MemToReg,
  output MemWrite,
  output ALUSrc,
  output RegWrite,
  output Jmp,
  output JAL,
  output ALUOp1,
  output ALUOp0,
  output ANDI
);

  wire and_4_out, and_5_out, and_6_out, and_7_out, and_8_out, and_9_out, and_11_out, and_12_out, and_13_out,
       not_1_out, not_2_out, not_3_out, not_4_out, not_5_out, not_6_out, not_7_out, not_8_out, not_9_out,
       not_10_out, not_11_out, not_12_out, not_13_out, not_14_out, not_15_out, not_16_out, not_17_out,
       not_18_out, not_19_out, not_20_out, not_21_out, not_22_out, not_23_out, not_24_out, not_25_out,
       not_26_out, not_27_out;

  not not_1 (not_1_out, Op1);
  not not_2 (not_2_out, Op3);
  not not_3 (not_3_out, Op3);
  and and_1 (MemWrite, Op5, Op3);
  or or_1 (ALUSrc, Op3, Op5);
  not not_4 (not_4_out, Op2);
  not not_5 (not_5_out, Op1);
  not not_6 (not_6_out, Op4);
  not not_7 (not_7_out, Op3);
  not not_8 (not_8_out, Op2);
  not not_9 (not_9_out, Op5);
  not not_10 (not_10_out, Op3);
  not not_11 (not_11_out, Op5);
  not not_12 (not_12_out, Op4);
  not not_13 (not_13_out, Op3);
  not not_14 (not_14_out, Op2);
  not not_15 (not_15_out, Op3);
  not not_16 (not_16_out, Op0);
  not not_17 (not_17_out, Op5);
  not not_18 (not_18_out, Op4);
  not not_19 (not_19_out, Op3);
  not not_20 (not_20_out, Op2);
  not not_21 (not_21_out, Op1);
  not not_22 (not_22_out, Op0);
  not not_23 (not_23_out, Op2);
  not not_24 (not_24_out, Op5);
  not not_25 (not_25_out, Op4);
  not not_26 (not_26_out, Op1);
  not not_27 (not_27_out, Op0);
  or or_2 (RegDst, not_1_out, Op3);
  and and_2 (Branch, not_2_out, Op2);
  and and_3 (MemRead, Op5, not_3_out);
  and and_4 (and_4_out, not_4_out, not_5_out);
  and and_5 (and_5_out, not_6_out, not_7_out, not_8_out, Op0);
  and and_6 (and_6_out, not_9_out, Op3);
  and and_7 (and_7_out, Op5, not_10_out);
  and and_8 (and_8_out, not_11_out, not_12_out, not_13_out, not_14_out, Op1);
  and and_9 (and_9_out, not_15_out, Op1, not_16_out);
  and and_10 (JAL, not_17_out, not_18_out, not_19_out, not_20_out, Op0);
  and and_11 (and_11_out, not_21_out, Op0);
  and and_12 (and_12_out, Op3, Op1, not_22_out);
  and and_13 (and_13_out, Op3, not_23_out);
  and and_14 (ANDI, not_24_out, not_25_out, Op3, Op2, not_26_out, not_27_out);
  or or_3 (RegWrite, and_4_out, and_5_out, and_6_out, and_7_out);
  or or_4 (Jmp, and_8_out, and_9_out);
  or or_5 (ALUOp1, and_11_out, and_12_out);
  or or_6 (ALUOp0, and_13_out, Op5);

  assign MemToReg = Op5;
endmodule

module ALU_Control (
  input  ALUOp1,
  input  ALUOp0,
  input  Funt1,
  input  Funt2,
  input  Funt3,
  input  Funt4,
  output ALUop1_2,
  output ALUop2,
  output ALUop3,
  output JR
);

  wire and_1_out, and_2_out, and_3_out, and_4_out, and_5_out, and_6_out, and_7_out, and_8_out, not_1_out,
       not_2_out, not_3_out, not_4_out, not_5_out, not_6_out, not_7_out, not_8_out, not_9_out, not_10_out,
       not_11_out, not_12_out, not_13_out, not_14_out, not_15_out, not_16_out, not_17_out, not_18_out,
       not_19_out, not_20_out, not_21_out;

  not not_1 (not_1_out, ALUOp0);
  not not_2 (not_2_out, Funt1);
  not not_3 (not_3_out, Funt2);
  not not_4 (not_4_out, ALUOp0);
  not not_5 (not_5_out, Funt1);
  not not_6 (not_6_out, ALUOp1);
  not not_7 (not_7_out, ALUOp0);
  not not_8 (not_8_out, Funt2);
  not not_9 (not_9_out, Funt4);
  not not_10 (not_10_out, ALUOp1);
  not not_11 (not_11_out, Funt3);
  not not_12 (not_12_out, Funt4);
  not not_13 (not_13_out, ALUOp1);
  not not_14 (not_14_out, Funt2);
  not not_15 (not_15_out, ALUOp1);
  not not_16 (not_16_out, ALUOp1);
  not not_17 (not_17_out, ALUOp0);
  not not_18 (not_18_out, Funt2);
  not not_19 (not_19_out, Funt3);
  not not_20 (not_20_out, Funt4);
  and and_1 (and_1_out, not_1_out, not_2_out, not_3_out);
  and and_2 (and_2_out, not_4_out, not_5_out, Funt4);
  and and_3 (and_3_out, not_6_out, ALUOp0);
  and and_4 (and_4_out, ALUOp1, not_7_out);
  and and_5 (and_5_out, not_8_out, not_9_out);
  not not_21 (not_21_out, Funt3);
  and and_6 (and_6_out, not_10_out, not_11_out, not_12_out);
  and and_7 (and_7_out, not_13_out, not_14_out, Funt4);
  and and_8 (and_8_out, not_15_out, ALUOp0);
  and and_9 (JR, not_16_out, not_17_out, Funt1, not_18_out, not_19_out, not_20_out);
  or or_1 (ALUop1_2, and_1_out, and_2_out, and_3_out, and_4_out);
  or or_2 (ALUop2, and_5_out, not_21_out, ALUOp0, ALUOp1);
  or or_3 (ALUop3, and_6_out, and_7_out, and_8_out);
endmodule
