// Logisim project Lab-3-CTRL-ALU-DONE - Copy.circ as structural Verilog: 4 circuits, main circuit Main
module Main (
  input  [5:0] in_1
);

  wire ALUSrcA, Branch, clock_1_out, clock_2_out, clock_3_out, clock_4_out, clock_5_out, clock_6_out,
       clock_7_out, clock_8_out, clock_9_out, IorD, IRWrite, JAL, JR, Jump, MemRead, MemWrite, or_1_out,
       PCEnable, PCWrite, PCWriteCond, RegWrite, Zero;
  wire [1:0] ALUSrcB, MemtoReg, PCSource, RegDst;
  wire [2:0] ALUop, NextStates;
  wire [3:0] ALUcntrl;
  wire [4:0] Write_Addr;
  wire [7:0] multiplexer_2_out;
  wire [23:0] rom_1_data;
  wire [27:0] bit_extender_2_out, shifter_2_out;
  wire [31:0] A_q, alu_1_aluresult, ALUout, bit_extender_1_out, INSTR, JRVal, MDR_q, MemData,
       multiplexer_1_out, multiplexer_5_out, multiplexer_6_out, NextPC, PC, ram_1_data,
       register_file_1_rddata2, shifter_1_out, Write_Data;

  Multiplexer #(.width(32), .enable("false")) multiplexer_1 (
    .in0(NextPC), .in1(JRVal), .out(multiplexer_1_out), .sel(JR));
  Register #(.width(32)) u_PC (.D(multiplexer_1_out), .en(PCEnable), .Q(PC), .clk(clock_1_out));  // open: clr
  Clock clock_1 (.out(clock_1_out));
  Multiplexer #(.width(8), .enable("false")) multiplexer_2 (
    .in0(PC[7:0]), .in1(ALUout[7:0]), .out(multiplexer_2_out), .sel(IorD));
  Clock clock_2 (.out(clock_2_out));
  // Probe on INSTR[31:26]
  RAM #(.dataWidth(32), .bus("separate")) ram_1 (
    .addr(multiplexer_2_out), .din(MemData), .data(ram_1_data), .str(MemWrite), .clk(clock_2_out),
    .ld(MemRead));  // open: sel, clr
  Register #(.width(32)) IR (.D(ram_1_data), .en(IRWrite), .Q(INSTR), .clk(clock_3_out));  // open: clr
  Clock clock_3 (.out(clock_3_out));
  Register #(.width(32)) MDR (.D(ram_1_data), .Q(MDR_q), .clk(clock_4_out));  // open: en, clr
  Clock clock_4 (.out(clock_4_out));
  ROM #(.addrWidth(9), .dataWidth(24)) rom_1 (.addr({NextStates, INSTR[31:26]}), .data(rom_1_data));  // open: sel
  Register #(.width(24)) register_1 (
    .D(rom_1_data),
    .Q({JAL, Jump, IRWrite, PCWriteCond, PCWrite, RegDst, ALUSrcA, MemRead, ALUop, IorD, ALUSrcB, MemWrite, PCSource, RegWrite, MemtoReg, NextStates}),
    .clk(clock_5_out));  // open: en, clr
  Clock clock_5 (.out(clock_5_out));
  Multiplexer #(.select(2), .width(5), .enable("false")) multiplexer_3 (
    .in0(INSTR[20:16]), .in1(INSTR[15:11]), .in2({5{1'b1}}), .out(Write_Addr), .sel(RegDst));  // open: in3
  Multiplexer #(.select(2), .width(32), .enable("false")) multiplexer_4 (
    .in0(ALUout), .in1(MDR_q), .in2(PC), .out(Write_Data), .sel(MemtoReg));  // open: in3
  Register_File register_file_1 (
    .WrAddr(Write_Addr), .WrData(Write_Data), .WrReg(RegWrite), .RdAddr1(INSTR[25:21]),
    .RdAddr2(INSTR[20:16]), .RdData1(JRVal), .RdData2(register_file_1_rddata2), .Clock(clock_6_out));
  Clock clock_6 (.out(clock_6_out));
  assign bit_extender_1_out = {{16{1'b0}}, INSTR[15:0]};  // Bit_Extender bit_extender_1
  // Probe on NextStates
  Shifter #(.width(32)) shifter_1 (.in(bit_extender_1_out), .\dist (5'b00010), .out(shifter_1_out));
  or or_1 (or_1_out, Branch, PCWrite);
  or or_2 (PCEnable, or_1_out, JR);
  Register #(.width(32)) A (.D(JRVal), .Q(A_q), .clk(clock_7_out));  // open: en, clr
  Clock clock_7 (.out(clock_7_out));
  Register #(.width(32)) B (.D(register_file_1_rddata2), .Q(MemData), .clk(clock_8_out));  // open: en, clr
  Clock clock_8 (.out(clock_8_out));
  // Probe on RegDst
  // Probe on MemtoReg
  // Probe on PCSource
  // Probe on ALUSrcB
  and and_1 (Branch, Zero, PCWriteCond);
  Multiplexer #(.width(32), .enable("false")) multiplexer_5 (
    .in0(PC), .in1(A_q), .out(multiplexer_5_out), .sel(ALUSrcA));
  Multiplexer #(.select(2), .width(32), .enable("false")) multiplexer_6 (
    .in0(MemData), .in1(32'h1), .in2(bit_extender_1_out), .in3(shifter_1_out), .out(multiplexer_6_out),
    .sel(ALUSrcB));
  ALU alu_1 (
    .ALUCtl(ALUcntrl), .A(multiplexer_5_out), .B(multiplexer_6_out), .ALUResult(alu_1_aluresult),
    .Zero(Zero), .Shamt(INSTR[10:6]));  // open: Overflow
  assign bit_extender_2_out = {{2{1'b0}}, INSTR[25:0]};  // Bit_Extender bit_extender_2
  // Probe on PC
  // Probe on Branch
  // Probe on Jump
  // Probe on JAL
  // Probe on JR
  // Probe on RegWrite
  // Probe on Write_Addr
  // Probe on Write_Data
  // Probe on MemWrite
  // Probe on MemData
  ROM #(.addrWidth(9), .dataWidth(5)) rom_2 (.addr({ALUop, INSTR[5:0]}), .data({JR, ALUcntrl}));  // open: sel
  Shifter #(.width(28)) shifter_2 (.in(bit_extender_2_out), .\dist (5'b00010), .out(shifter_2_out));
  Register #(.width(32)) u_ALUout (.D(alu_1_aluresult), .Q(ALUout), .clk(clock_9_out));  // open: en, clr
  Clock clock_9 (.out(clock_9_out));
  Multiplexer #(.select(2), .width(32), .enable("false")) multiplexer_7 (
    .in0(alu_1_aluresult), .in1(ALUout), .in2({PC[31:28], shifter_2_out}), .out(NextPC), .sel(PCSource));  // open: in3

  // Other names for the same wires on the sheet: RdAddr2[4:0] = INSTR[20:16]

  // Notes on the sheet:
  //   contents of rom_1 (hex, n*v repeats v):
  //   288201 0 282201 282201 288201 0 0 0 288201 0 288201 0 288201 288201 21*0 288201 7*0 288201 20*0 602
  //   0 602 202 602 0 0 0 602 0 602 0 602 602 21*0 602 7*0 602 20*0 12003 0 480080 8c00b0 111040 0 0 0
  //   10403 0 13403 0 15403 13403 21*0 10403 7*0 10403 20*0 20020 7*0 20020 0 20020 0 20020 20020 21*0
  //   8804 7*0 900 55*0 28
  //   contents of rom_2 (hex, n*v repeats v):
  //   64*7 64*5 9 0 8 5*0 17 23*0 7 0 0 5 3 2 0 4 0 0 2 1 20*0 64*6 64*2 64*3
endmodule

module ALU (
  input  [3:0] ALUCtl,
  input  [31:0] A,
  input  [31:0] B,
  input  [4:0] Shamt,
  output [31:0] ALUResult,
  output Zero,
  output Overflow
);

  wire comparator_1_lt, comparator_2_lt, comparator_3_eq, comparator_4_eq, or_2_out;
  wire [31:0] ADD, AND, NOR, OR, SLL, SLT, SLTU, SRL, SUB, XOR;

  // Probe on ALUCtl
  assign NOR = ~(A | B);  // NOR_Gate nor_1, 32 bits wide
  Adder #(.width(32)) adder_1 (.a(A), .b(B), .out(ADD));  // open: cin, cout
  Subtractor #(.width(32)) subtractor_1 (.a(A), .b(B), .out(SUB));  // open: bin, bout
  assign AND = A & B;  // AND_Gate and_1, 32 bits wide
  assign OR = A | B;  // OR_Gate or_1, 32 bits wide
  assign XOR = A ^ B;  // XOR_Gate xor_1, 32 bits wide
  Comparator #(.width(32)) comparator_1 (.a(A), .b(B), .lt(comparator_1_lt));  // open: gt, eq
  assign SLT = {{31{1'b0}}, comparator_1_lt};  // Bit_Extender bit_extender_1
  Shifter #(.width(32)) shifter_1 (.in(B), .\dist (Shamt), .out(SLL));
  Shifter #(.width(32), .shift("lr")) shifter_2 (.in(B), .\dist (Shamt), .out(SRL));
  Comparator #(.width(32), .mode("unsigned")) comparator_2 (.a(A), .b(B), .lt(comparator_2_lt));  // open: gt, eq
  assign SLTU = {{31{1'b0}}, comparator_2_lt};  // Bit_Extender bit_extender_2
  Multiplexer #(.select(4), .width(32), .enable("false")) multiplexer_1 (
    .in0(XOR), .in1(SLTU), .in2(SLT), .in3(AND), .in4(NOR), .in5(SUB), .in6(OR), .in7(ADD), .in8(SRL),
    .in9(SLL), .out(ALUResult), .sel(ALUCtl));  // open: in10, in11, in12, in13, in14, in15
  Comparator #(.width(4)) comparator_3 (.a(4'b0111), .b(ALUCtl), .eq(comparator_3_eq));  // open: gt, lt
  Comparator #(.width(4)) comparator_4 (.a(ALUCtl), .b(4'b0101), .eq(comparator_4_eq));  // open: gt, lt
  Overflow_Unit overflow_unit_1 (
    .Add(comparator_3_eq), .Sub(comparator_4_eq), .ASign(A[31]), .BSign(B[31]), .ResultSign(ALUResult[31]),
    .Overflow(Overflow));
  or or_2 (or_2_out, ALUResult[0], ALUResult[1], ALUResult[2], ALUResult[3], ALUResult[4], ALUResult[5], ALUResult[6], ALUResult[7], ALUResult[8], ALUResult[9], ALUResult[10], ALUResult[11], ALUResult[12], ALUResult[13], ALUResult[14], ALUResult[15], ALUResult[16], ALUResult[17], ALUResult[18], ALUResult[19], ALUResult[20], ALUResult[21], ALUResult[22], ALUResult[23], ALUResult[24], ALUResult[25], ALUResult[26], ALUResult[27], ALUResult[28], ALUResult[29], ALUResult[30], ALUResult[31]);
  not not_1 (Zero, or_2_out);

  // Other names for the same wires on the sheet: ASign = A[31]; ResultSign = ALUResult[31]; BSign = B[31]

  // Notes on the sheet:
  //   ALUCtl for ADD for top port
  //   ALUCtl for SUB for second port
endmodule

module Register_File (
  input  [4:0] WrAddr,
  input  [31:0] WrData,
  input  WrReg,
  input  [4:0] RdAddr1,
  input  [4:0] RdAddr2,
  input  Clock,
  output [31:0] RdData1,
  output [31:0] RdData2
);

  wire WrReg0, WrReg1, WrReg2, WrReg3, WrReg4, WrReg5, WrReg6, WrReg7, WrReg8, WrReg9, WrReg10, WrReg11,
       WrReg12, WrReg13, WrReg14, WrReg15, WrReg16, WrReg17, WrReg18, WrReg19, WrReg20, WrReg21, WrReg22,
       WrReg23, WrReg24, WrReg25, WrReg26, WrReg27, WrReg28, WrReg29, WrReg30, WrReg31;
  wire [31:0] RegData1, RegData2, RegData3, RegData4, RegData5, RegData6, RegData7, RegData8, RegData9,
       RegData10, RegData11, RegData12, RegData13, RegData14, RegData15, RegData16, RegData17, RegData18,
       RegData19, RegData20, RegData21, RegData22, RegData23, RegData24, RegData25, RegData26, RegData27,
       RegData28, RegData29, RegData30, RegData31;

  Demultiplexer #(.select(5), .enable("false")) demultiplexer_1 (
    .out0(WrReg0), .out1(WrReg1), .out2(WrReg2), .out3(WrReg3), .out4(WrReg4), .out5(WrReg5), .out6(WrReg6),
    .out7(WrReg7), .out8(WrReg8), .out9(WrReg9), .out10(WrReg10), .out11(WrReg11), .out12(WrReg12),
    .out13(WrReg13), .out14(WrReg14), .out15(WrReg15), .out16(WrReg16), .out17(WrReg17), .out18(WrReg18),
    .out19(WrReg19), .out20(WrReg20), .out21(WrReg21), .out22(WrReg22), .out23(WrReg23), .out24(WrReg24),
    .out25(WrReg25), .out26(WrReg26), .out27(WrReg27), .out28(WrReg28), .out29(WrReg29), .out30(WrReg30),
    .out31(WrReg31), .in(WrReg), .sel(WrAddr));
  // Probe on RegData4
  Register #(.width(32)) Reg4 (.D(WrData), .en(WrReg4), .Q(RegData4), .clk(Clock));  // open: clr
  // Probe on RegData8
  Register #(.width(32)) Reg8 (.D(WrData), .en(WrReg8), .Q(RegData8), .clk(Clock));  // open: clr
  // Probe on RegData12
  Register #(.width(32)) Reg12 (.D(WrData), .en(WrReg12), .Q(RegData12), .clk(Clock));  // open: clr
  // Probe on RegData16
  Register #(.width(32)) Reg16 (.D(WrData), .en(WrReg16), .Q(RegData16), .clk(Clock));  // open: clr
  // Probe on RegData20
  Register #(.width(32)) Reg20 (.D(WrData), .en(WrReg20), .Q(RegData20), .clk(Clock));  // open: clr
  // Probe on RegData24
  Register #(.width(32)) Reg24 (.D(WrData), .en(WrReg24), .Q(RegData24), .clk(Clock));  // open: clr
  // Probe on RegData28
  Register #(.width(32)) Reg28 (.D(WrData), .en(WrReg28), .Q(RegData28), .clk(Clock));  // open: clr
  Register #(.width(32)) Reg1 (.D(WrData), .en(WrReg1), .Q(RegData1), .clk(Clock));  // open: clr
  Register #(.width(32)) Reg5 (.D(WrData), .en(WrReg5), .Q(RegData5), .clk(Clock));  // open: clr
  Register #(.width(32)) Reg9 (.D(WrData), .en(WrReg9), .Q(RegData9), .clk(Clock));  // open: clr
  Register #(.width(32)) Reg13 (.D(WrData), .en(WrReg13), .Q(RegData13), .clk(Clock));  // open: clr
  Register #(.width(32)) Reg17 (.D(WrData), .en(WrReg17), .Q(RegData17), .clk(Clock));  // open: clr
  Register #(.width(32)) Reg21 (.D(WrData), .en(WrReg21), .Q(RegData21), .clk(Clock));  // open: clr
  Register #(.width(32)) Reg25 (.D(WrData), .en(WrReg25), .Q(RegData25), .clk(Clock));  // open: clr
  Register #(.width(32)) Reg29 (.D(WrData), .en(WrReg29), .Q(RegData29), .clk(Clock));  // open: clr
  // Probe on RegData1
  // Probe on RegData5
  // Probe on RegData9
  // Probe on RegData13
  // Probe on RegData17
  // Probe on RegData21
  // Probe on RegData25
  // Probe on RegData29
  // Probe on RegData2
  Register #(.width(32)) Reg2 (.D(WrData), .en(WrReg2), .Q(RegData2), .clk(Clock));  // open: clr
  // Probe on RegData6
  Register #(.width(32)) Reg6 (.D(WrData), .en(WrReg6), .Q(RegData6), .clk(Clock));  // open: clr
  // Probe on RegData10
  Register #(.width(32)) Reg10 (.D(WrData), .en(WrReg10), .Q(RegData10), .clk(Clock));  // open: clr
  // Probe on RegData14
  Register #(.width(32)) Reg14 (.D(WrData), .en(WrReg14), .Q(RegData14), .clk(Clock));  // open: clr
  // Probe on RegData18
  Register #(.width(32)) Reg18 (.D(WrData), .en(WrReg18), .Q(RegData18), .clk(Clock));  // open: clr
  // Probe on RegData22
  Register #(.width(32)) Reg22 (.D(WrData), .en(WrReg22), .Q(RegData22), .clk(Clock));  // open: clr
  // Probe on RegData26
  Register #(.width(32)) Reg26 (.D(WrData), .en(WrReg26), .Q(RegData26), .clk(Clock));  // open: clr
  // Probe on RegData30
  Register #(.width(32)) Reg30 (.D(WrData), .en(WrReg30), .Q(RegData30), .clk(Clock));  // open: clr
  // Probe on RegData3
  Register #(.width(32)) Reg3 (.D(WrData), .en(WrReg3), .Q(RegData3), .clk(Clock));  // open: clr
  // Probe on RegData7
  Register #(.width(32)) Reg7 (.D(WrData), .en(WrReg7), .Q(RegData7), .clk(Clock));  // open: clr
  // Probe on RegData11
  Register #(.width(32)) Reg11 (.D(WrData), .en(WrReg11), .Q(RegData11), .clk(Clock));  // open: clr
  // Probe on RegData15
  Register #(.width(32)) Reg15 (.D(WrData), .en(WrReg15), .Q(RegData15), .clk(Clock));  // open: clr
  // Probe on RegData19
  Register #(.width(32)) Reg19 (.D(WrData), .en(WrReg19), .Q(RegData19), .clk(Clock));  // open: clr
  // Probe on RegData23
  Register #(.width(32)) Reg23 (.D(WrData), .en(WrReg23), .Q(RegData23), .clk(Clock));  // open: clr
  // Probe on RegData27
  Register #(.width(32)) Reg27 (.D(WrData), .en(WrReg27), .Q(RegData27), .clk(Clock));  // open: clr
  // Probe on RegData31
  Register #(.width(32)) Reg31 (.D(WrData), .en(WrReg31), .Q(RegData31), .clk(Clock));  // open: clr
  Multiplexer #(.select(5), .width(32), .enable("false")) multiplexer_1 (
    .in0({32{1'b0}}), .in1(RegData1), .in2(RegData2), .in3(RegData3), .in4(RegData4), .in5(RegData5),
    .in6(RegData6), .in7(RegData7), .in8(RegData8), .in9(RegData9), .in10(RegData10), .in11(RegData11),
    .in12(RegData12), .in13(RegData13), .in14(RegData14), .in15(RegData15), .in16(RegData16),
    .in17(RegData17), .in18(RegData18), .in19(RegData19), .in20(RegData20), .in21(RegData21),
    .in22(RegData22), .in23(RegData23), .in24(RegData24), .in25(RegData25), .in26(RegData26),
    .in27(RegData27), .in28(RegData28), .in29(RegData29), .in30(RegData30), .in31(RegData31), .out(RdData1),
    .sel(RdAddr1));
  Multiplexer #(.select(5), .width(32), .enable("false")) multiplexer_2 (
    .in0({32{1'b0}}), .in1(RegData1), .in2(RegData2), .in3(RegData3), .in4(RegData4), .in5(RegData5),
    .in6(RegData6), .in7(RegData7), .in8(RegData8), .in9(RegData9), .in10(RegData10), .in11(RegData11),
    .in12(RegData12), .in13(RegData13), .in14(RegData14), .in15(RegData15), .in16(RegData16),
    .in17(RegData17), .in18(RegData18), .in19(RegData19), .in20(RegData20), .in21(RegData21),
    .in22(RegData22), .in23(RegData23), .in24(RegData24), .in25(RegData25), .in26(RegData26),
    .in27(RegData27), .in28(RegData28), .in29(RegData29), .in30(RegData30), .in31(RegData31), .out(RdData2),
    .sel(RdAddr2));
endmodule

module Overflow_Unit (
  input  Add,
  input  Sub,
  input  ASign,
  input  BSign,
  input  ResultSign,
  output Overflow
);

  wire and_1_out, and_2_out, or_1_out, xnor_1_out, xor_1_out, xor_2_out;

  xnor xnor_1 (xnor_1_out, ASign, BSign);
  xor xor_1 (xor_1_out, ASign, BSign);
  and and_1 (and_1_out, xnor_1_out, Add);
  and and_2 (and_2_out, xor_1_out, Sub);
  or or_1 (or_1_out, and_1_out, and_2_out);
  xor xor_2 (xor_2_out, ResultSign, ASign);
  and and_3 (Overflow, or_1_out, xor_2_out);

  // Notes on the sheet:
  //   Overflow occurs when doing addition and sign(A) == sign(B) && sign(result) != sign(A)
  //   Or
  //   Overflow occurs when doing subtraction and sign(A) != sign(B) && sign(result) != sign(A)
endmodule
