// Logisim project Lab-4-Given.circ as structural Verilog: 7 circuits, main circuit Main
module Main (
  output [4:0] out_1,
  output [31:0] out_2,
  output [5:0] out_3
);

  wire ALUSrc, and_1_out, Branch, CLK, EX_Mem_WrReg, Hazard, JAL, JR, Jump, LW_stall, Mem_WB_2_q, memRead,
       MemToReg, memWrtie, not_1_out, not_2_out, not_3_out, or_2_out, RegDst, Stall, WrReg, Zero;
  wire [0:0] Ex_Mem_q;
  wire [1:0] FwdA, FwdB;
  wire [2:0] ALUop;
  wire [3:0] ALU_Cntrl_alu_cntrl, ALUCntrl, ID_Ex_q;
  wire [4:0] Ex_Mem_4_q, ID_EX_RS, ID_ExRD_q, ID_ExRT_q, multiplexer_8_out, Shamt, WrAddr;
  wire [5:0] bit_extender_2_out;
  wire [8:0] rom_1_data;
  wire [15:0] ID_ExRS_2_q;
  wire [27:0] bit_extender_1_out, JumpV;
  wire [31:0] alu_1_aluresult, Branch_target, DataA, DataB, ID_Ex_2_q, ID_Ex_3_q, ID_Ex_4_q, JALval, JRVal,
       Mem_WB_3_q, MemData, multiplexer_1_out, multiplexer_2_out, multiplexer_5_out, multiplexer_6_out,
       multiplexer_7_out, multiplexer_9_out, NextPC, PC, PC_Branch, ram_1_data, register_file_1_rddata2,
       rom_2_data, shifter_2_out, WrData;
  wire [31:6] bit_extender_2_out_2;

  Clock clock_1 (.out(CLK));
  Register #(.width(32)) u_PC (.D(NextPC), .en(not_1_out), .Q(PC), .clk(CLK));  // open: clr
  not not_1 (not_1_out, Stall);
  ROM #(.addrWidth(6), .dataWidth(12)) rom_1 (
    .addr(out_2[31:26]), .data({Branch, Jump, JAL, rom_1_data[8], ALUop, rom_1_data[4:0]}));  // open: sel
  Adder #(.width(32)) adder_1 (.a(PC), .b(32'h1), .out(JALval));  // open: cin, cout
  Hazard_detection_unit Hazard_Dectection_Unit (
    .Branch(Branch), .Zero(Zero), .Jump(Jump), .JAL(JAL), .JR(JR), .FWDA(FwdA), .FWDB(FwdB), .LW(LW_stall),
    .Hazard(Hazard), .Stall(Stall));
  not not_2 (not_2_out, Stall);
  Multiplexer #(.width(32), .enable("false")) multiplexer_1 (
    .in0(JALval), .in1(JRVal), .out(multiplexer_1_out), .sel(JR));
  ROM #(.dataWidth(32)) rom_2 (.addr(PC[7:0]), .data(rom_2_data));  // open: sel
  Register #(.width(6)) ID_Ex (
    .D({rom_1_data[8], rom_1_data[4:0]}), .en(not_2_out), .Q({RegDst, ALUSrc, ID_Ex_q}), .clk(CLK),
    .clr(Hazard));
  Multiplexer #(.width(32), .enable("false")) multiplexer_2 (
    .in0(multiplexer_1_out), .in1({JALval[31:28], JumpV}), .out(multiplexer_2_out), .sel(Jump));
  not not_3 (not_3_out, Stall);
  and and_1 (and_1_out, Branch, Zero);
  Register #(.width(32)) IF_ID (.D(JALval), .en(not_3_out), .Q(PC_Branch), .clk(CLK), .clr(Hazard));
  Register #(.width(32)) IF_ID_2 (.D(rom_2_data), .en(not_3_out), .Q(out_2), .clk(CLK), .clr(Hazard));
  Register #(.width(4)) Ex_Mem (
    .D(ID_Ex_q), .Q({memRead, memWrtie, EX_Mem_WrReg, Ex_Mem_q[0]}), .clk(CLK));  // open: en, clr
  Multiplexer #(.width(32), .enable("false")) multiplexer_3 (
    .in0(multiplexer_2_out), .in1(Branch_target), .out(NextPC), .sel(and_1_out));
  assign bit_extender_1_out = {{2{1'b0}}, out_2[25:0]};  // Bit_Extender bit_extender_1
  Register #(.width(2)) Mem_WB (.D({EX_Mem_WrReg, Ex_Mem_q[0]}), .Q({WrReg, MemToReg}), .clk(CLK));  // open: en, clr
  Register #(.width(1)) Mem_WB_2 (.D(memRead), .Q(Mem_WB_2_q), .clk(CLK));  // open: en, clr
  Multiplexer #(.width(5), .enable("false")) multiplexer_4 (.in0(WrAddr), .in1({5{1'b1}}), .out(out_1), .sel(JAL));
  Multiplexer #(.width(32), .enable("false")) multiplexer_5 (
    .in0(WrData), .in1(JALval), .out(multiplexer_5_out), .sel(JAL));
  assign {bit_extender_2_out_2, bit_extender_2_out} = {{16{1'b0}}, out_2[15:0]};  // Bit_Extender bit_extender_2
  or or_1 (LW_stall, Mem_WB_2_q, ID_Ex_q[3], memRead);
  or or_2 (or_2_out, WrReg, JAL);
  Shifter #(.width(28)) shifter_1 (.in(bit_extender_1_out), .\dist (5'b00010), .out(JumpV));
  Shifter #(.width(32)) shifter_2 (
    .in({bit_extender_2_out_2, bit_extender_2_out}), .\dist (5'b00010), .out(shifter_2_out));
  Register_File register_file_1 (
    .WrAddr(out_1), .WrData(multiplexer_5_out), .WrReg(or_2_out), .RdAddr1(out_2[25:21]),
    .RdAddr2(out_2[20:16]), .RdData1(JRVal), .RdData2(register_file_1_rddata2), .Clock(CLK));
  Adder #(.width(32)) adder_2 (.a(shifter_2_out), .b(PC_Branch), .out(Branch_target));  // open: cin, cout
  Comparator #(.width(32)) comparator_1 (.a(JRVal), .b(register_file_1_rddata2), .eq(Zero));  // open: gt, lt
  ALUcntrl ALU_Cntrl (.Funct(bit_extender_2_out), .ALUop(ALUop), .ALU_Cntrl(ALU_Cntrl_alu_cntrl), .JR(JR));
  Register #(.width(5)) ID_ExRT (.D(out_2[20:16]), .Q(ID_ExRT_q), .clk(CLK), .clr(Stall));  // open: en
  Register #(.width(5)) ID_ExRD (.D(out_2[15:11]), .Q(ID_ExRD_q), .clk(CLK), .clr(Stall));  // open: en
  Register #(.width(5)) ID_ExRS (.D(out_2[25:21]), .Q(ID_EX_RS), .clk(CLK), .clr(Stall));  // open: en
  Register #(.width(16)) ID_ExRS_2 (
    .D(out_2[15:0]), .Q({ID_ExRS_2_q[15:11], Shamt, ID_ExRS_2_q[5:0]}), .clk(CLK), .clr(Stall));  // open: en
  Register #(.width(32)) ID_Ex_2 (.D(JRVal), .Q(ID_Ex_2_q), .clk(CLK), .clr(Stall));  // open: en
  Register #(.width(32)) ID_Ex_3 (.D(register_file_1_rddata2), .Q(ID_Ex_3_q), .clk(CLK), .clr(Stall));  // open: en
  Multiplexer #(.select(2), .width(32), .enable("false")) multiplexer_6 (
    .in0(ID_Ex_3_q), .in1(DataB), .in2(DataA), .out(multiplexer_6_out), .sel(FwdB));  // open: in3
  Register #(.width(32)) ID_Ex_4 (
    .D({bit_extender_2_out_2, bit_extender_2_out}), .Q(ID_Ex_4_q), .clk(CLK), .clr(Stall));  // open: en
  Register #(.width(4)) ID_Ex_5 (.D(ALU_Cntrl_alu_cntrl), .Q(ALUCntrl), .clk(CLK), .clr(Stall));  // open: en
  Multiplexer #(.select(2), .width(32), .enable("false")) multiplexer_7 (
    .in0(ID_Ex_2_q), .in1(DataB), .in2(DataA), .out(multiplexer_7_out), .sel(FwdA));  // open: in3
  Multiplexer #(.width(5), .enable("false")) multiplexer_8 (
    .in0(ID_ExRT_q), .in1(ID_ExRD_q), .out(multiplexer_8_out), .sel(RegDst));
  Multiplexer #(.width(32), .enable("false")) multiplexer_9 (
    .in0(multiplexer_6_out), .in1(ID_Ex_4_q), .out(multiplexer_9_out), .sel(ALUSrc));
  ALU alu_1 (
    .ALUCtl(ALUCntrl), .A(multiplexer_7_out), .B(multiplexer_9_out), .ALUResult(alu_1_aluresult),
    .Shamt(Shamt));  // open: Zero, Overflow
  Register #(.width(32)) Ex_Mem_2 (.D(alu_1_aluresult), .Q(DataA), .clk(CLK));  // open: en, clr
  Register #(.width(32)) Ex_Mem_3 (.D(multiplexer_6_out), .Q(MemData), .clk(CLK));  // open: en, clr
  Register #(.width(5)) Ex_Mem_4 (.D(multiplexer_8_out), .Q(Ex_Mem_4_q), .clk(CLK));  // open: en, clr
  Forwarding_Unit forwarding_unit_1 (
    .Ex_MEM_RegWrite(EX_Mem_WrReg), .Ex_MEM_RegRD(Ex_Mem_4_q), .ID_Ex_RegRs(ID_EX_RS),
    .ID_Ex_RegRt(ID_ExRT_q), .MEM_WB_RegWrite(WrReg), .MEM_WB_RegRD(WrAddr), .ForwardA(FwdA), .ForwardB(FwdB));
  RAM #(.dataWidth(32), .bus("separate")) ram_1 (
    .addr(DataA[7:0]), .din(MemData), .data(ram_1_data), .str(memWrtie), .clk(CLK), .ld(memRead));  // open: sel, clr
  Register #(.width(32)) Mem_WB_3 (.D(ram_1_data), .Q(Mem_WB_3_q), .clk(CLK));  // open: en, clr
  Register #(.width(32)) Mem_WB_4 (.D(DataA), .Q(DataB), .clk(CLK));  // open: en, clr
  Register #(.width(5)) Mem_WB_5 (.D(Ex_Mem_4_q), .Q(WrAddr), .clk(CLK));  // open: en, clr
  Multiplexer #(.width(32), .enable("false")) multiplexer_10 (
    .in0(DataB), .in1(Mem_WB_3_q), .out(WrData), .sel(MemToReg));
  // Probe on PC
  // Probe on Branch
  // Probe on Jump
  // Probe on JAL
  // Probe on JR
  // Probe on WrReg
  // Probe on WrAddr
  // Probe on WrData
  // Probe on memWrtie
  // Probe on MemData

  assign out_3 = out_2[31:26];

  // Other names for the same wires on the sheet: JumpV[31:28] = JALval[31:28]; Split[15:0] = out_2[15:0];
  //   RD[4:0] = out_2[15:11]; RT[4:0] = out_2[20:16]; RS[4:0] = out_2[25:21]; OpCntrl[5:0] = out_2[31:26]

  // Notes on the sheet:
  //   contents of rom_1 (hex, n*v repeats v):
  //   142 0 400 600 800 0 0 0 32 0 92 0 b2 72 21*0 1b 7*0 14
  //   Instruction Memory
  //   contents of rom_2 (hex, n*v repeats v):
  //   34010001 211020 221826 2064000e 232822 aca4000e 8ca6000e c43824 10e10003 c7402a 11080001 201a0001
  //   20090001 8c0a000c ad4a0013 8c0a000c 1141fffb c000013 201b0001 23ff0034 ac1f0000 308b0010 456027
  //   446825 97140 27842 28900014 25882b 8c120000 2400008 201c0001 800001f 201d0001 201e0001
  //   Data Memory
endmodule

module ALU (
  input  [3:0] ALUCtl,
  input  [31:0] A,
  input  [31:0] B,
  input  [4:0] Shamt,
  output [31:0] ALUResult,
  output Zero,
  output Overflow
);

  wire comparator_1_lt, comparator_2_lt, comparator_3_eq, comparator_4_eq, or_2_out;
  wire [31:0] ADD, AND, NOR, OR, SLL, SLT, SLTU, SRL, SUB, XOR;

  assign XOR = A ^ B;  // XOR_Gate xor_1, 32 bits wide
  Adder #(.width(32)) adder_1 (.a(A), .b(B), .out(ADD));  // open: cin, cout
  Subtractor #(.width(32)) subtractor_1 (.a(A), .b(B), .out(SUB));  // open: bin, bout
  assign AND = A & B;  // AND_Gate and_1, 32 bits wide
  assign OR = A | B;  // OR_Gate or_1, 32 bits wide
  assign NOR = ~(A | B);  // NOR_Gate nor_1, 32 bits wide
  Comparator #(.width(32)) comparator_1 (.a(A), .b(B), .lt(comparator_1_lt));  // open: gt, eq
  assign SLT = {{31{1'b0}}, comparator_1_lt};  // Bit_Extender bit_extender_1
  Shifter #(.width(32)) shifter_1 (.in(B), .\dist (Shamt), .out(SLL));
  Shifter #(.width(32), .shift("lr")) shifter_2 (.in(B), .\dist (Shamt), .out(SRL));
  Comparator #(.width(32), .mode("unsigned")) comparator_2 (.a(A), .b(B), .lt(comparator_2_lt));  // open: gt, eq
  assign SLTU = {{31{1'b0}}, comparator_2_lt};  // Bit_Extender bit_extender_2
  Multiplexer #(.select(4), .width(32), .enable("false")) multiplexer_1 (
    .in0(XOR), .in1(SLTU), .in2(SLT), .in3(AND), .in4(NOR), .in5(SUB), .in6(OR), .in7(ADD), .in8(SRL),
    .in9(SLL), .out(ALUResult), .sel(ALUCtl));  // open: in10, in11, in12, in13, in14, in15
  Comparator #(.width(4)) comparator_3 (.a(4'b0111), .b(ALUCtl), .eq(comparator_3_eq));  // open: gt, lt
  Comparator #(.width(4)) comparator_4 (.a(ALUCtl), .b(4'b0101), .eq(comparator_4_eq));  // open: gt, lt
  Overflow_Unit overflow_unit_1 (
    .Add(comparator_3_eq), .Sub(comparator_4_eq), .ASign(A[31]), .BSign(B[31]), .ResultSign(ALUResult[31]),
    .Overflow(Overflow));
  or or_2 (or_2_out, ALUResult[0], ALUResult[1], ALUResult[2], ALUResult[3], ALUResult[4], ALUResult[5], ALUResult[6], ALUResult[7], ALUResult[8], ALUResult[9], ALUResult[10], ALUResult[11], ALUResult[12], ALUResult[13], ALUResult[14], ALUResult[15], ALUResult[16], ALUResult[17], ALUResult[18], ALUResult[19], ALUResult[20], ALUResult[21], ALUResult[22], ALUResult[23], ALUResult[24], ALUResult[25], ALUResult[26], ALUResult[27], ALUResult[28], ALUResult[29], ALUResult[30], ALUResult[31]);
  not not_1 (Zero, or_2_out);

  // Other names for the same wires on the sheet: ASign = A[31]; ResultSign = ALUResult[31]; BSign = B[31]

  // Notes on the sheet:
  //   ALUCtl for ADD on top port
  //   ALUCtl for SUB on second port
endmodule

module Register_File (
  input  [4:0] WrAddr,
  input  [31:0] WrData,
  input  WrReg,
  input  [4:0] RdAddr1,
  input  [4:0] RdAddr2,
  input  Clock,
  output [31:0] RdData1,
  output [31:0] RdData2
);

  wire and_1_out, and_2_out, comparator_1_eq, comparator_2_eq, comparator_3_eq, comparator_4_eq, not_1_out,
       not_2_out, WrReg0, WrReg1, WrReg2, WrReg3, WrReg4, WrReg5, WrReg6, WrReg7, WrReg8, WrReg9, WrReg10,
       WrReg11, WrReg12, WrReg13, WrReg14, WrReg15, WrReg16, WrReg17, WrReg18, WrReg19, WrReg20, WrReg21,
       WrReg22, WrReg23, WrReg24, WrReg25, WrReg26, WrReg27, WrReg28, WrReg29, WrReg30, WrReg31;
  wire [31:0] multiplexer_1_out, multiplexer_2_out, RegData1, RegData2, RegData3, RegData4, RegData5,
       RegData6, RegData7, RegData8, RegData9, RegData10, RegData11, RegData12, RegData13, RegData14,
       RegData15, RegData16, RegData17, RegData18, RegData19, RegData20, RegData21, RegData22, RegData23,
       RegData24, RegData25, RegData26, RegData27, RegData28, RegData29, RegData30, RegData31;

  Demultiplexer #(.select(5), .enable("false")) demultiplexer_1 (
    .out0(WrReg0), .out1(WrReg1), .out2(WrReg2), .out3(WrReg3), .out4(WrReg4), .out5(WrReg5), .out6(WrReg6),
    .out7(WrReg7), .out8(WrReg8), .out9(WrReg9), .out10(WrReg10), .out11(WrReg11), .out12(WrReg12),
    .out13(WrReg13), .out14(WrReg14), .out15(WrReg15), .out16(WrReg16), .out17(WrReg17), .out18(WrReg18),
    .out19(WrReg19), .out20(WrReg20), .out21(WrReg21), .out22(WrReg22), .out23(WrReg23), .out24(WrReg24),
    .out25(WrReg25), .out26(WrReg26), .out27(WrReg27), .out28(WrReg28), .out29(WrReg29), .out30(WrReg30),
    .out31(WrReg31), .in(WrReg), .sel(WrAddr));
  // Probe on RegData4
  Register #(.width(32)) Reg4 (.D(WrData), .en(WrReg4), .Q(RegData4), .clk(Clock));  // open: clr
  // Probe on RegData8
  Register #(.width(32)) Reg8 (.D(WrData), .en(WrReg8), .Q(RegData8), .clk(Clock));  // open: clr
  // Probe on RegData12
  Register #(.width(32)) Reg12 (.D(WrData), .en(WrReg12), .Q(RegData12), .clk(Clock));  // open: clr
  // Probe on RegData16
  Register #(.width(32)) Reg16 (.D(WrData), .en(WrReg16), .Q(RegData16), .clk(Clock));  // open: clr
  // Probe on RegData20
  Register #(.width(32)) Reg20 (.D(WrData), .en(WrReg20), .Q(RegData20), .clk(Clock));  // open: clr
  // Probe on RegData24
  Register #(.width(32)) Reg24 (.D(WrData), .en(WrReg24), .Q(RegData24), .clk(Clock));  // open: clr
  // Probe on RegData28
  Register #(.width(32)) Reg28 (.D(WrData), .en(WrReg28), .Q(RegData28), .clk(Clock));  // open: clr
  Register #(.width(32)) Reg1 (.D(WrData), .en(WrReg1), .Q(RegData1), .clk(Clock));  // open: clr
  Register #(.width(32)) Reg5 (.D(WrData), .en(WrReg5), .Q(RegData5), .clk(Clock));  // open: clr
  Register #(.width(32)) Reg9 (.D(WrData), .en(WrReg9), .Q(RegData9), .clk(Clock));  // open: clr
  Register #(.width(32)) Reg13 (.D(WrData), .en(WrReg13), .Q(RegData13), .clk(Clock));  // open: clr
  Register #(.width(32)) Reg17 (.D(WrData), .en(WrReg17), .Q(RegData17), .clk(Clock));  // open: clr
  Register #(.width(32)) Reg21 (.D(WrData), .en(WrReg21), .Q(RegData21), .clk(Clock));  // open: clr
  Register #(.width(32)) Reg25 (.D(WrData), .en(WrReg25), .Q(RegData25), .clk(Clock));  // open: clr
  Register #(.width(32)) Reg29 (.D(WrData), .en(WrReg29), .Q(RegData29), .clk(Clock));  // open: clr
  // Probe on RegData1
  // Probe on RegData5
  // Probe on RegData9
  // Probe on RegData13
  // Probe on RegData17
  // Probe on RegData21
  // Probe on RegData25
  // Probe on RegData29
  // Probe on RegData2
  Register #(.width(32)) Reg2 (.D(WrData), .en(WrReg2), .Q(RegData2), .clk(Clock));  // open: clr
  // Probe on RegData6
  Register #(.width(32)) Reg6 (.D(WrData), .en(WrReg6), .Q(RegData6), .clk(Clock));  // open: clr
  // Probe on RegData10
  Register #(.width(32)) Reg10 (.D(WrData), .en(WrReg10), .Q(RegData10), .clk(Clock));  // open: clr
  // Probe on RegData14
  Register #(.width(32)) Reg14 (.D(WrData), .en(WrReg14), .Q(RegData14), .clk(Clock));  // open: clr
  // Probe on RegData18
  Register #(.width(32)) Reg18 (.D(WrData), .en(WrReg18), .Q(RegData18), .clk(Clock));  // open: clr
  // Probe on RegData22
  Register #(.width(32)) Reg22 (.D(WrData), .en(WrReg22), .Q(RegData22), .clk(Clock));  // open: clr
  // Probe on RegData26
  Register #(.width(32)) Reg26 (.D(WrData), .en(WrReg26), .Q(RegData26), .clk(Clock));  // open: clr
  // Probe on RegData30
  Register #(.width(32)) Reg30 (.D(WrData), .en(WrReg30), .Q(RegData30), .clk(Clock));  // open: clr
  // Probe on RegData3
  Register #(.width(32)) Reg3 (.D(WrData), .en(WrReg3), .Q(RegData3), .clk(Clock));  // open: clr
  // Probe on RegData7
  Register #(.width(32)) Reg7 (.D(WrData), .en(WrReg7), .Q(RegData7), .clk(Clock));  // open: clr
  // Probe on RegData11
  Register #(.width(32)) Reg11 (.D(WrData), .en(WrReg11), .Q(RegData11), .clk(Clock));  // open: clr
  // Probe on RegData15
  Register #(.width(32)) Reg15 (.D(WrData), .en(WrReg15), .Q(RegData15), .clk(Clock));  // open: clr
  // Probe on RegData19
  Register #(.width(32)) Reg19 (.D(WrData), .en(WrReg19), .Q(RegData19), .clk(Clock));  // open: clr
  // Probe on RegData23
  Register #(.width(32)) Reg23 (.D(WrData), .en(WrReg23), .Q(RegData23), .clk(Clock));  // open: clr
  // Probe on RegData27
  Register #(.width(32)) Reg27 (.D(WrData), .en(WrReg27), .Q(RegData27), .clk(Clock));  // open: clr
  // Probe on RegData31
  Register #(.width(32)) Reg31 (.D(WrData), .en(WrReg31), .Q(RegData31), .clk(Clock));  // open: clr
  Multiplexer #(.select(5), .width(32), .enable("false")) multiplexer_1 (
    .in0({32{1'b0}}), .in1(RegData1), .in2(RegData2), .in3(RegData3), .in4(RegData4), .in5(RegData5),
    .in6(RegData6), .in7(RegData7), .in8(RegData8), .in9(RegData9), .in10(RegData10), .in11(RegData11),
    .in12(RegData12), .in13(RegData13), .in14(RegData14), .in15(RegData15), .in16(RegData16),
    .in17(RegData17), .in18(RegData18), .in19(RegData19), .in20(RegData20), .in21(RegData21),
    .in22(RegData22), .in23(RegData23), .in24(RegData24), .in25(RegData25), .in26(RegData26),
    .in27(RegData27), .in28(RegData28), .in29(RegData29), .in30(RegData30), .in31(RegData31),
    .out(multiplexer_1_out), .sel(RdAddr1));
  Multiplexer #(.select(5), .width(32), .enable("false")) multiplexer_2 (
    .in0({32{1'b0}}), .in1(RegData1), .in2(RegData2), .in3(RegData3), .in4(RegData4), .in5(RegData5),
    .in6(RegData6), .in7(RegData7), .in8(RegData8), .in9(RegData9), .in10(RegData10), .in11(RegData11),
    .in12(RegData12), .in13(RegData13), .in14(RegData14), .in15(RegData15), .in16(RegData16),
    .in17(RegData17), .in18(RegData18), .in19(RegData19), .in20(RegData20), .in21(RegData21),
    .in22(RegData22), .in23(RegData23), .in24(RegData24), .in25(RegData25), .in26(RegData26),
    .in27(RegData27), .in28(RegData28), .in29(RegData29), .in30(RegData30), .in31(RegData31),
    .out(multiplexer_2_out), .sel(RdAddr2));
  Multiplexer #(.width(32), .enable("false")) multiplexer_3 (
    .in0(multiplexer_1_out), .in1(WrData), .out(RdData1), .sel(and_1_out));
  Comparator #(.width(5), .mode("unsigned")) comparator_1 (
    .a(WrAddr), .b(RdAddr2), .eq(comparator_1_eq));  // open: gt, lt
  Multiplexer #(.width(32), .enable("false")) multiplexer_4 (
    .in0(multiplexer_2_out), .in1(WrData), .out(RdData2), .sel(and_2_out));
  Comparator #(.width(5), .mode("unsigned")) comparator_2 (
    .a(WrAddr), .b(RdAddr1), .eq(comparator_2_eq));  // open: gt, lt
  and and_1 (and_1_out, comparator_2_eq, WrReg, not_1_out);
  and and_2 (and_2_out, comparator_1_eq, WrReg, not_2_out);
  Comparator #(.width(5), .mode("unsigned")) comparator_3 (
    .a(WrAddr), .b({5{1'b0}}), .eq(comparator_3_eq));  // open: gt, lt
  not not_1 (not_1_out, comparator_3_eq);
  Comparator #(.width(5), .mode("unsigned")) comparator_4 (
    .a(WrAddr), .b({5{1'b0}}), .eq(comparator_4_eq));  // open: gt, lt
  not not_2 (not_2_out, comparator_4_eq);
endmodule

module Overflow_Unit (
  input  Add,
  input  Sub,
  input  ASign,
  input  BSign,
  input  ResultSign,
  output Overflow
);

  wire and_1_out, and_2_out, or_1_out, xnor_1_out, xor_1_out, xor_2_out;

  xnor xnor_1 (xnor_1_out, ASign, BSign);
  xor xor_1 (xor_1_out, ASign, BSign);
  and and_1 (and_1_out, xnor_1_out, Add);
  and and_2 (and_2_out, xor_1_out, Sub);
  or or_1 (or_1_out, and_1_out, and_2_out);
  xor xor_2 (xor_2_out, ResultSign, ASign);
  and and_3 (Overflow, or_1_out, xor_2_out);

  // Notes on the sheet:
  //   Overflow occurs when doing addition and sign(A) == sign(B) && sign(result) != sign(A)
  //   Or
  //   Overflow occurs when doing subtraction and sign(A) != sign(B) && sign(result) != sign(A)
endmodule

module Forwarding_Unit (
  input  Ex_MEM_RegWrite,
  input  [4:0] Ex_MEM_RegRD,
  input  [4:0] ID_Ex_RegRs,
  input  [4:0] ID_Ex_RegRt,
  input  MEM_WB_RegWrite,
  input  [4:0] MEM_WB_RegRD,
  output [1:0] ForwardA,
  output [1:0] ForwardB
);

  wire and_1_out, and_2_out, and_3_out, and_4_out, comparator_1_eq, comparator_2_eq, comparator_3_eq,
       comparator_4_eq, comparator_5_eq, comparator_6_eq, comparator_7_eq, comparator_8_eq, not_1_out,
       not_2_out, not_3_out, not_4_out;
  wire [1:0] multiplexer_1_out, multiplexer_2_out;

  Comparator #(.width(5)) comparator_1 (.a(Ex_MEM_RegRD), .b({5{1'b0}}), .eq(comparator_1_eq));  // open: gt, lt
  Comparator #(.width(5)) comparator_2 (.a(Ex_MEM_RegRD), .b(ID_Ex_RegRs), .eq(comparator_2_eq));  // open: gt, lt
  not not_1 (not_1_out, comparator_3_eq);
  Comparator #(.width(5)) comparator_3 (.a(MEM_WB_RegRD), .b({5{1'b0}}), .eq(comparator_3_eq));  // open: gt, lt
  Comparator #(.width(5)) comparator_4 (.a(MEM_WB_RegRD), .b(ID_Ex_RegRs), .eq(comparator_4_eq));  // open: gt, lt
  Comparator #(.width(5)) comparator_5 (.a(Ex_MEM_RegRD), .b({5{1'b0}}), .eq(comparator_5_eq));  // open: gt, lt
  not not_2 (not_2_out, comparator_5_eq);
  Comparator #(.width(5)) comparator_6 (.a(Ex_MEM_RegRD), .b(ID_Ex_RegRt), .eq(comparator_6_eq));  // open: gt, lt
  not not_3 (not_3_out, comparator_1_eq);
  and and_1 (and_1_out, MEM_WB_RegWrite, not_1_out, comparator_4_eq);
  and and_2 (and_2_out, Ex_MEM_RegWrite, not_2_out, comparator_6_eq);
  and and_3 (and_3_out, Ex_MEM_RegWrite, not_3_out, comparator_2_eq);
  Comparator #(.width(5)) comparator_7 (.a(MEM_WB_RegRD), .b({5{1'b0}}), .eq(comparator_7_eq));  // open: gt, lt
  Comparator #(.width(5)) comparator_8 (.a(MEM_WB_RegRD), .b(ID_Ex_RegRt), .eq(comparator_8_eq));  // open: gt, lt
  not not_4 (not_4_out, comparator_7_eq);
  and and_4 (and_4_out, MEM_WB_RegWrite, not_4_out, comparator_8_eq);
  Multiplexer #(.width(2), .enable("false")) multiplexer_1 (
    .in0(2'b00), .in1(2'b01), .out(multiplexer_1_out), .sel(and_4_out));
  Multiplexer #(.width(2), .enable("false")) multiplexer_2 (
    .in0(2'b00), .in1(2'b01), .out(multiplexer_2_out), .sel(and_1_out));
  Multiplexer #(.width(2), .enable("false")) multiplexer_3 (
    .in0(multiplexer_2_out), .in1(2'b10), .out(ForwardA), .sel(and_3_out));
  Multiplexer #(.width(2), .enable("false")) multiplexer_4 (
    .in0(multiplexer_1_out), .in1(2'b10), .out(ForwardB), .sel(and_2_out));
endmodule

module ALUcntrl (
  input  [5:0] Funct,
  input  [2:0] ALUop,
  output [3:0] ALU_Cntrl,
  output JR
);

  ROM #(.addrWidth(9), .dataWidth(5)) rom_1 (.addr({ALUop, Funct}), .data({JR, ALU_Cntrl}));  // open: sel

  // Notes on the sheet:
  //   contents of rom_1 (hex, n*v repeats v):
  //   128*7 9 0 8 5*0 17 23*0 7 0 5 5 3 6 0 4 0 0 2 1 20*0 64*6 64*2 64*3
endmodule

module Hazard_detection_unit (
  input  Branch,
  input  Zero,
  input  Jump,
  input  JAL,
  input  JR,
  input  [1:0] FWDA,
  input  [1:0] FWDB,
  input  LW,
  output Hazard,
  output Stall
);

  wire and_1_out, comparator_1_eq, comparator_2_eq, not_1_out, not_2_out, or_1_out;

  and and_1 (and_1_out, Branch, Zero);
  Comparator #(.width(2)) comparator_1 (.a(FWDA), .b(2'b00), .eq(comparator_1_eq));  // open: gt, lt
  Comparator #(.width(2)) comparator_2 (.a(FWDB), .b(2'b00), .eq(comparator_2_eq));  // open: gt, lt
  not not_1 (not_1_out, comparator_1_eq);
  or or_1 (or_1_out, not_1_out, not_2_out);
  not not_2 (not_2_out, comparator_2_eq);
  and and_2 (Stall, or_1_out, LW);
  or or_2 (Hazard, and_1_out, Jump, JAL, JR);
endmodule
